# Fritzing sketch Dino_Game_Breadboard (saved by Fritzing 1.0.4)
breadboards: 1

parts:
  Part1 = Black Joystick KY-023
  Mod1 = ESP32-TTGO-T-DISPLAY
  R2 = Resistor [tolerance=±5% power=0.25W resistance=220 package=THT]
  LED1 = LED - 5mm [color="Red (633nm)" current=0.030A package="5 mm [THT]"]
  S1 = Pushbutton [package="[THT]"]
  R4 = 12mm Trimmer Potentiometer (Large) [maximum_resistance=10kΩ knob_status=50% power=0.5W package=THT]

nets:
  N1: Part1.SW, Mod1.33
  N2: Part1.VRy, Mod1.32
  N3: Part1.VRx, Mod1.39
  N4: Part1.+5V, Mod1.3V, R4.leg2
  N5: Part1.GND, Mod1.G-1, Mod1.G-2, Mod1.G-10, Mod1.G-11, Mod1.G-14, R2.Pin_0, LED1.cathode, S1.Pin_3, S1.Pin_4, R4.leg1
  N6: Mod1.2, S1.Pin_1, S1.Pin_2
  N7: Mod1.15, R2.Pin_1
  N8: Mod1.13, R4.wiper

custom parts:
  Black Joystick KY-023: Description: The joystick is a combination of 2 analoog potentiometer and a digital switch. Arduino GND --> Module pin - Arduino +5V --> Module pin +5V Arduino Analoog 0 --> Module VRx Arduino Analoog 1 --> Module VRy Arduino Digital --> Module SW Dimensions: 1" x 1.25"
  ESP32-TTGO-T-DISPLAY: LILYGO TTGO T-Display GD32VF103CBT6 Main Chip ST7789 1.14 Inch IPS 240x135 Resolution Minimalist Development Board.
